// Logisim project CPU.circ as structural Verilog: 11 circuits, main circuit full_adder
module main (
  input  PB,
  input  AL,
  input  AE,
  input  EO,
  input  SU,
  input  IL,
  input  IE,
  input  BL,
  input  BE
);

  wire ALU_c, clock_1_out;
  wire [7:0] A_st, ALU_st, B_st, dipswitch_1_sw8, IR_q;

  Clock clock_1 (.out(clock_1_out));
  DipSwitch dipswitch_1 (
    .sw1(dipswitch_1_sw8[7]), .sw2(dipswitch_1_sw8[6]), .sw3(dipswitch_1_sw8[5]), .sw4(dipswitch_1_sw8[4]),
    .sw5(dipswitch_1_sw8[3]), .sw6(dipswitch_1_sw8[2]), .sw7(dipswitch_1_sw8[1]), .sw8(dipswitch_1_sw8[0]));
  register_8_bit IR (.D(IR_q), .L(IL), .E(IE), .CLK(clock_1_out), .Q(IR_q));  // open: ST
  assign IR_q = PB ? dipswitch_1_sw8 : 8'bz;  // Controlled_Buffer controlled_buffer_1
  LedBar ledbar_1 (
    .led0(IR_q[7]), .led1(IR_q[6]), .led2(IR_q[5]), .led3(IR_q[4]), .led4(IR_q[3]), .led5(IR_q[2]),
    .led6(IR_q[1]), .led7(IR_q[0]));
  register_8_bit A (.D(IR_q), .L(AL), .E(AE), .CLK(clock_1_out), .Q(IR_q), .ST(A_st));
  arithmetic_unit_8_bit ALU (.A(A_st), .B(B_st), .EO(EO), .SU(SU), .Q(IR_q), .C(ALU_c), .ST(ALU_st));
  register_8_bit B (.D(IR_q), .L(BL), .E(BE), .CLK(clock_1_out), .Q(IR_q), .ST(B_st));
  LedBar ledbar_2 (
    .led0(A_st[7]), .led1(A_st[6]), .led2(A_st[5]), .led3(A_st[4]), .led4(A_st[3]), .led5(A_st[2]),
    .led6(A_st[1]), .led7(A_st[0]));
  LedBar ledbar_3 (
    .led0(ALU_st[7]), .led1(ALU_st[6]), .led2(ALU_st[5]), .led3(ALU_st[4]), .led4(ALU_st[3]),
    .led5(ALU_st[2]), .led6(ALU_st[1]), .led7(ALU_st[0]));
  LedBar ledbar_4 (
    .led0(B_st[7]), .led1(B_st[6]), .led2(B_st[5]), .led3(B_st[4]), .led4(B_st[3]), .led5(B_st[2]),
    .led6(B_st[1]), .led7(B_st[0]));
  LED led_1 (.in(ALU_c));
endmodule

module half_adder (
  input  A,
  input  B,
  output Co,
  output O
);

  and and_1 (Co, A, B);
  xor xor_1 (O, A, B);
endmodule

module full_adder (
  input  Ci,
  input  A,
  input  B,
  output Co,
  output O
);

  wire and_1_out, and_2_out, xor_1_out;

  xor xor_1 (xor_1_out, A, B);
  and and_1 (and_1_out, A, B);
  or or_1 (Co, and_1_out, and_2_out);
  and and_2 (and_2_out, Ci, xor_1_out);
  xor xor_2 (O, Ci, xor_1_out);
endmodule

module adder_8_bit (
  input  Ci,
  input  [7:0] A,
  input  [7:0] B,
  output [7:0] O,
  output C
);

  wire full_adder_1_co, full_adder_2_co, full_adder_3_co, full_adder_4_co, full_adder_5_co, full_adder_6_co,
       full_adder_7_co;

  full_adder full_adder_1 (.Ci(Ci), .A(A[0]), .B(B[0]), .Co(full_adder_1_co), .O(O[0]));
  full_adder full_adder_2 (.Ci(full_adder_1_co), .A(A[1]), .B(B[1]), .Co(full_adder_2_co), .O(O[1]));
  full_adder full_adder_3 (.Ci(full_adder_2_co), .A(A[2]), .B(B[2]), .Co(full_adder_3_co), .O(O[2]));
  full_adder full_adder_4 (.Ci(full_adder_3_co), .A(A[3]), .B(B[3]), .Co(full_adder_4_co), .O(O[3]));
  full_adder full_adder_5 (.Ci(full_adder_4_co), .A(A[4]), .B(B[4]), .Co(full_adder_5_co), .O(O[4]));
  full_adder full_adder_6 (.Ci(full_adder_5_co), .A(A[5]), .B(B[5]), .Co(full_adder_6_co), .O(O[5]));
  full_adder full_adder_7 (.Ci(full_adder_6_co), .A(A[6]), .B(B[6]), .Co(full_adder_7_co), .O(O[6]));
  full_adder full_adder_8 (.Ci(full_adder_7_co), .A(A[7]), .B(B[7]), .Co(C), .O(O[7]));
endmodule

module or_latch (
  input  S,
  output Q
);

  or or_1 (Q, S, Q);
endmodule

module sr_latch (
  input  R,
  input  S,
  output Q,
  output NQ
);

  nor nor_1 (Q, R, NQ);
  nor nor_2 (NQ, Q, S);
endmodule

module d_latch (
  input  D,
  input  E,
  output Q,
  output NQ
);

  wire and_1_out, and_2_out, not_1_out;

  not not_1 (not_1_out, D);
  and and_1 (and_1_out, not_1_out, E);
  and and_2 (and_2_out, E, D);
  sr_latch sr_latch_1 (.R(and_1_out), .S(and_2_out), .Q(Q), .NQ(NQ));
endmodule

module d_flip_flop (
  input  D,
  input  RCLK,
  output Q,
  output NQ
);

  D_Flip_Flop d_ff_1 (.D(D), .clk(RCLK), .Q(Q), .Qn(NQ));  // open: preset, reset
endmodule

module register_1_bit (
  input  D,
  input  E,
  input  CLK,
  output Q
);

  wire and_1_out, and_2_out, not_1_out, or_1_out;

  not not_1 (not_1_out, E);
  and and_1 (and_1_out, Q, not_1_out);
  and and_2 (and_2_out, D, E);
  or or_1 (or_1_out, and_1_out, and_2_out);
  d_flip_flop d_flip_flop_1 (.D(or_1_out), .RCLK(CLK), .Q(Q));  // open: NQ
endmodule

module register_8_bit (
  input  [7:0] D,
  input  L,
  input  E,
  input  CLK,
  output [7:0] Q,
  output [7:0] ST
);

  register_1_bit register_1_bit_1 (.D(D[0]), .E(L), .CLK(CLK), .Q(ST[0]));
  register_1_bit register_1_bit_2 (.D(D[1]), .E(L), .CLK(CLK), .Q(ST[1]));
  register_1_bit register_1_bit_3 (.D(D[2]), .E(L), .CLK(CLK), .Q(ST[2]));
  register_1_bit register_1_bit_4 (.D(D[3]), .E(L), .CLK(CLK), .Q(ST[3]));
  register_1_bit register_1_bit_5 (.D(D[4]), .E(L), .CLK(CLK), .Q(ST[4]));
  register_1_bit register_1_bit_6 (.D(D[5]), .E(L), .CLK(CLK), .Q(ST[5]));
  register_1_bit register_1_bit_7 (.D(D[6]), .E(L), .CLK(CLK), .Q(ST[6]));
  register_1_bit register_1_bit_8 (.D(D[7]), .E(L), .CLK(CLK), .Q(ST[7]));
  assign Q = E ? ST : 8'bz;  // Controlled_Buffer controlled_buffer_1
endmodule

module arithmetic_unit_8_bit (
  input  [7:0] A,
  input  [7:0] B,
  input  EO,
  input  SU,
  output [7:0] Q,
  output C,
  output [7:0] ST
);

  wire [7:0] xor_8_out;

  xor xor_1 (xor_8_out[7], SU, B[7]);
  xor xor_2 (xor_8_out[6], SU, B[6]);
  xor xor_3 (xor_8_out[5], SU, B[5]);
  xor xor_4 (xor_8_out[4], SU, B[4]);
  xor xor_5 (xor_8_out[3], SU, B[3]);
  adder_8_bit adder_8_bit_1 (.Ci(SU), .A(A), .B(xor_8_out), .O(ST), .C(C));
  xor xor_6 (xor_8_out[2], SU, B[2]);
  assign Q = EO ? ST : 8'bz;  // Controlled_Buffer controlled_buffer_1
  xor xor_7 (xor_8_out[1], SU, B[1]);
  xor xor_8 (xor_8_out[0], SU, B[0]);
endmodule
